# Fritzing sketch On-Air-LIght (saved by Fritzing 0.9.9b)
breadboards: 1

parts:
  MH-ET_LIVE_ESP32_DEVKIT1 = MH-ET LIVE ESP32 DEVKIT 38 pins
  LED1 = RGB LED (com. anode, rbg) [package="5 mm [THT]"]
  LED2 = RGB LED (com. anode, rbg) [package="5 mm [THT]"]

nets:
  N1: MH-ET_LIVE_ESP32_DEVKIT1.3V3, LED1.common_anode, LED2.common_anode
  N2: MH-ET_LIVE_ESP32_DEVKIT1.IO14, LED1.blue_cathode, LED2.blue_cathode
  N3: MH-ET_LIVE_ESP32_DEVKIT1.IO12, LED1.red_cathode, LED2.red_cathode
  N4: MH-ET_LIVE_ESP32_DEVKIT1.IO13, LED1.green_cathode, LED2.green_cathode

custom parts:
  MH-ET LIVE ESP32 DEVKIT 38 pins: http://mh.nodebb.com/topic/2/mh-et-live-esp32-devkit
